# Fritzing sketch schematics (saved by Fritzing 0.9.3b)

parts:
  DHT1 = DHT22 Humidity and Temperature Sensor
  PIR1 = PIR sensor
  Part1 = MQ-4
  WeMos_D1_Mini1 = WeMos D1 Mini

nets:
  VDD: DHT1.VDD, PIR1.VDD, Part1.VCC, WeMos_D1_Mini1.5V
  N1: DHT1.DATA, WeMos_D1_Mini1.D5
  GND: DHT1.GND, PIR1.GND, Part1.GND, WeMos_D1_Mini1.G
  N2: PIR1.SIG, WeMos_D1_Mini1.D0
  N3: Part1.AO, WeMos_D1_Mini1.A0

notes:
  Actually MQ-135, check pin labels on device (red VCC, black GND, green A0
  Note: gas sensor heats up. Mount accordingly!
  Temperature sensor should be mounted far from heat-generating elements (gas sensor, ESP)
  Mount PIR sensor to front of the enclosure (cut appropriate hole for the lens). Ensure isolation between contacts and microcontroller
